// Logisim project logisim_is_back.circ as structural Verilog
module main (
  input  in_1,
  input  in_2,
  output out_3
);

  Adder #(.width(1)) adder_1 (.a(in_1), .b(in_2), .out(out_3));  // open: cin, cout
endmodule

module AND_GATE (
  input  in_1,
  input  in_2,
  output out_3
);

  Multiplier #(.width(1)) multiplier_1 (.a(in_1), .b(in_2), .out(out_3));  // open: cin, cout
endmodule

module Clock_work (
  input  in_1
);

  wire buzzer_1_p7, clock_1_out, comparator_1_eq, comparator_2_eq, comparator_3_eq, comparator_4_eq,
       comparator_5_eq, j_k_ff_1_q, j_k_ff_2_q, n7_segment_display_1_p1, n7_segment_display_2_p1,
       n7_segment_display_3_p1;
  wire [7:0] counter_1_q;

  Clock clock_1 (.out(clock_1_out));
  Counter #(.max('hf)) counter_1 (.clr(in_1), .clk(clock_1_out), .Q(counter_1_q));  // open: load, up, count, D, carry
  // BCD_to_7_Segment_decoder bcd_to_7_segment_decoder_1: pin names not known
  // BCD_to_7_Segment_decoder bcd_to_7_segment_decoder_2: pin names not known
  // _7_Segment_Display 7_segment_display_1: pin names not known; wires that end beside it: n7_segment_display_1_p1, n7_segment_display_1_p1
  // _7_Segment_Display 7_segment_display_2: pin names not known; wires that end beside it: n7_segment_display_2_p1, n7_segment_display_2_p1
  // Binary_to_BCD_converter #(.binvalue(8)) binary_to_bcd_converter_1: pin names not known; wires that end beside it: counter_1_q
  // BCD_to_7_Segment_decoder bcd_to_7_segment_decoder_3: pin names not known
  // _7_Segment_Display 7_segment_display_3: pin names not known; wires that end beside it: n7_segment_display_3_p1, n7_segment_display_3_p1
  LED led_1 (.in(comparator_1_eq));
  Comparator comparator_1 (.a({8{1'b0}}), .b(counter_1_q), .eq(comparator_1_eq));  // open: gt, lt
  Comparator comparator_2 (.a(8'h3), .b(counter_1_q), .eq(comparator_2_eq));  // open: gt, lt
  Comparator comparator_3 (.a(8'hf), .b(counter_1_q), .eq(comparator_3_eq));  // open: gt, lt
  Comparator comparator_4 (.a(8'h4), .b(counter_1_q), .eq(comparator_4_eq));  // open: gt, lt
  Comparator comparator_5 (.a(8'h7), .b(counter_1_q), .eq(comparator_5_eq));  // open: gt, lt
  J_K_Flip_Flop j_k_ff_1 (
    .J(comparator_2_eq), .K(comparator_3_eq), .clk(clock_1_out), .Q(j_k_ff_1_q));  // open: Qn, preset, reset
  // Buzzer buzzer_1: pin names not known; wires that end beside it: 8'h3, 8'hf, 8'h4, 8'h7, 14'h533, comparator_1_eq, buzzer_1_p7, buzzer_1_p7
  J_K_Flip_Flop j_k_ff_2 (
    .J(comparator_4_eq), .K(comparator_5_eq), .clk(clock_1_out), .Q(j_k_ff_2_q));  // open: Qn, preset, reset
  LED led_2 (.in(j_k_ff_1_q));
  // Digital_Oscilloscope #(.nState(20)) digital_oscilloscope_1: pin names not known; wires that end beside it: clock_1_out, comparator_1_eq, j_k_ff_1_q, j_k_ff_2_q
  LED led_3 (.in(j_k_ff_2_q));
  // Buzzer #(.vol_width(32)) buzzer_2: pin names not known; wires that end beside it: 14'h533, j_k_ff_1_q
  // Buzzer buzzer_3: pin names not known; wires that end beside it: 14'h533, j_k_ff_2_q
endmodule
